# Fritzing sketch circuit (saved by Fritzing 0.8.7b)

parts:
  Load_Cell1 = Load Cell - Red/white/black/green
  Part1 = HX711 Weighing Sensor Module
  Part2 = Arduino Uno (Rev3)
  Part3 = SRF05 Ultrasonic Rangefinder
  J1 = Basic Servo
  Display1 = LCD screen 16x2 IIC [part_number=101290]
  S1 = Pushbutton [package="[THT]"]
  LED1 = LED - 5mm [color="Red (633nm)" package="5 mm [THT]"]
  R1 = Resistor [tolerance=±5% resistance=330 package=THT]  # not connected
  R2 = Resistor [tolerance=±5% resistance=1k package=THT]
  J2 = Basic Servo

nets:
  N1: Load_Cell1.wire1, Part1.E+
  N2: Load_Cell1.wire2, Part1.A+
  N3: Load_Cell1.wire3, Part1.E-
  N4: Load_Cell1.wire4, Part1.A-
  VCC: Part1.VCC, Part2.5V
  GND: Part1.GND, Part2.GND, J1.gnd, J2.gnd
  N5: Part1.DO/RX, Part2.D2
  N6: Part1.CK/TX, Part2.D3_PWM
  N7: Part2.A4/SDA, Display1.SDA
  N8: Part2.A5/SCL, Display1.SCL
  N9: Part2.D10_PWM/SS, J2.pulse
  VCC_2: Part2.D13/SCK, J1.vcc, LED1.cathode, J2.vcc
  N10: Part2.D4, Part3.Echo
  N11: Part2.D5_PWM, Part3.Trig
  N12: Part2.D6_PWM, S1.Pin_3, R2.Pin_0
  N13: Part3.GND, R2.Pin_1

custom parts:
  Load Cell - Red/white/black/green: A rectangle load cell/weighting pressure Sensor with four wires - Red, white, black, green. Normally corresponding with E+, E-, A+, A- respectively.
  HX711 Weighing Sensor Module: HX711 is a precision 24-bit analog-to-digital converter (ADC) designed for weigh scales and industrial control applications to interface directly with a bridge sensor.
  LCD screen 16x2 IIC: LCD screen with HD44780 controller enables showing text, symbols, value or anything else that comes from Croduino/Arduino. It is capable of showing 16 symbols in two lines and therefore can be used in many projects that need to send clearly visible and legible output information.. • Color of symbols: White • Backlight: Blue • Dimensions: 80 x 36 x 12 mm • Screen dimensions: 64.5 x 16 mm •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
