# Fritzing sketch fruit-counter-circuit (saved by Fritzing 0.8.7b)

parts:
  Part2 = Arduino Uno (Rev3)
  Part3 = SRF05 Ultrasonic Rangefinder
  Display1 = LCD screen 16x2 IIC [part_number=101290]
  S1 = Pushbutton [package="[THT]"]
  LED1 = LED - 5mm [color="Red (633nm)" package="5 mm [THT]"]
  e-radionica1 = TCS230 Color Sensor [part_number=101209]
  J1 = Basic Servo
  J2 = Basic Servo
  R3 = Resistor [tolerance=±5% resistance=330 package=THT]
  R4 = Resistor [tolerance=±5% resistance=330 package=THT]
  Load_Cell3 = Load Cell - Red/white/black/green
  Part7 = HX711 Weighing Sensor Module

nets:
  N1: Part2.A4/SDA, Display1.SDA
  N2: Part2.A5/SCL, Display1.SCL
  N3: Part2.D8, e-radionica1.Out
  N4: Part2.D9_PWM, J2.pulse
  N5: Part2.D10_PWM/SS, J1.pulse
  N6: Part2.D11_PWM/MOSI, Part7.CK/TX
  N7: Part2.D12/MISO, Part7.DO/RX
  N8: Part2.D13/SCK, LED1.cathode
  GND: Part2.GND, Part3.GND, Display1.GND, e-radionica1.Gnd, J1.gnd, J2.gnd, R3.Pin_1, Part7.GND
  N9: Part2.D2, Part3.Trig
  N10: Part2.D3_PWM, Part3.Echo
  N11: Part2.D4, e-radionica1.S0
  N12: Part2.D5_PWM, e-radionica1.S1
  N13: Part2.D6_PWM, e-radionica1.S2
  N14: Part2.D7, e-radionica1.S3
  VCC: Part2.5V, Part3.VCC, Display1.VCC, S1.Pin_1, S1.Pin_2, e-radionica1.Vcc, J1.vcc, J2.vcc, R4.Pin_1, Part7.VCC
  N15: S1.Pin_3, S1.Pin_4, R3.Pin_0
  N16: LED1.anode, R4.Pin_0
  N17: Load_Cell3.wire1, Part7.E+
  N18: Load_Cell3.wire2, Part7.A+
  N19: Load_Cell3.wire3, Part7.E-
  N20: Load_Cell3.wire4, Part7.A-

custom parts:
  LCD screen 16x2 IIC: LCD screen with HD44780 controller enables showing text, symbols, value or anything else that comes from Croduino/Arduino. It is capable of showing 16 symbols in two lines and therefore can be used in many projects that need to send clearly visible and legible output information.. • Color of symbols: White • Backlight: Blue • Dimensions: 80 x 36 x 12 mm • Screen dimensions: 64.5 x 16 mm •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
  TCS230 Color Sensor: TCS230
  Load Cell - Red/white/black/green: A rectangle load cell/weighting pressure Sensor with four wires - Red, white, black, green. Normally corresponding with E+, E-, A+, A- respectively.
  HX711 Weighing Sensor Module: HX711 is a precision 24-bit analog-to-digital converter (ADC) designed for weigh scales and industrial control applications to interface directly with a bridge sensor.
